# Fritzing sketch lab3-schematic (saved by Fritzing 1.0.1rc)
breadboards: 1

parts:
  Part1 = Arduino Mega 2560 (Rev3)
  IC1 = L293D [package=THT]
  M1 = DC Motor [voltage_(max)=6V voltage_(min)=3V]
  R1 = Resistor [tolerance=±5% power=0.25W resistance=10k package=THT]
  U1 = LCD-16X2 [package=lcd-8x2-kit]
  Part2 = Adafruit DS1307 RTC Breakout [part_number="Adafruit #264"]
  MIC = KY-037 Sound Sensor Module [package="Breakout board"]

nets:
  N1: Part1.SCL, Part2.SCL
  N2: Part1.SDA, Part2.SDA
  N3: Part1.D9_PWM, MIC.D0
  D8: Part1.D8_PWM, U1.VO
  5V: Part1.VIN, IC1.+Vmotor, R1.Pin_0, U1.VDD, U1.A, MIC.+
  D3: Part1.D2_PWM, U1.E
  D2: Part1.D3_PWM, U1.RS
  D4: Part1.D4_PWM, U1.DB4
  D5: Part1.D5_PWM, U1.DB5
  D6: Part1.D6_PWM, IC1.In_2, U1.DB6
  D7: Part1.D7_PWM, IC1.In_1, U1.DB7
  N4: IC1.Enable_1, R1.Pin_1
  N5: IC1.Out_1_(_Controlled_by_Enable_1_), M1.pin_1
  GND: IC1.0V, U1.VSS, U1.R_W, U1.K, Part2.GND, MIC.G
  N6: IC1.Out_2_(_Controlled_by_Enable_1_), M1.pin_2
  3.3V: Part2.VCC
  A0: MIC.A0

custom parts:
  Adafruit DS1307 RTC Breakout: This is a great battery-backed real time clock (RTC) that allows your microcontroller project to keep track of time even if it is reprogrammed, or if the power is lost. Perfect for datalogging, clock-building, time stamping, timers and alarms, etc. The DS1307 is the most popular RTC - but it requires 5V power to work (although we've used it with 5V power and 3.3V logic successfully) PCB &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
  KY-037 Sound Sensor Module: Microphone Sound Sensor. It reacts on specific sound volume (Digital Output).
